# Fritzing sketch stepper_motor_wiring (saved by Fritzing 0.9.3b)
breadboards: 1

parts:
  LED1 = LED - 3mm [color="Green (565nm)" package="3 mm [THT]"]
  R3 = Resistor [tolerance=±5% resistance=100 package=THT]
  LCD1 = LCD screen  # not connected
  J1 = screw terminal, 5 pins
  Part3 = EasyDriver_v44
  M2 = Stepper Motor - Bipolar
  M3 = Stepper Motor - Bipolar
  Part4 = Photon
  DRV_1 = DRV 8825 Stepper Motor Carrier, High Current [part_number="DRV 8825"]  # not connected

nets:
  N1: LED1.cathode, J1.pin5
  N2: LED1.anode, R3.Pin_1
  GND: Part3.GND, Part4.GND
  N3: Part3.STEP, Part4.D4
  N4: Part3.DIR, Part4.D3
  N5: Part3.OUT2A, M2.A, M3.A
  N6: Part3.OUT2B, M2.C, M3.C
  N7: Part3.OUT1A, M2.B, M3.B
  N8: Part3.OUT1B, M2.D, M3.D
  N9: Part3.MS1, Part4.D5
  N10: Part3.ENABLE, Part4.D2
  N11: Part3.MS2, Part4.D6

notes:
  LCD Backpack
  LAT
  DAT
  CLK
  5V
  GND
  This should be the Big Easy Driver (BED), not just easydriver but the part does not exist yet (pins are very similar though)s
  This is the color coding for the KNF diaphragm pump
  Online steppers
  Gearbox 5:1
  MS3
