# Fritzing sketch stepper_particle_pcb (saved by Fritzing 0.9.3b)
circuit board: 8cm x 4.8cm
breadboards: 1

parts:
  Particle_Photon = Photon
  J11 = Screw terminal - 2 pins [package=THT]
  J12 = Screw terminal - 2 pins [package=THT]
  J13 = Screw terminal - 2 pins [package=THT]
  J2_Keypad_4x6 = male pin header, 4 pins [form="♂ (male)"]
  D2 = Rectifier Diode [part_number=1N4001 package="300 mil [THT]"]
  MD09B2 = Pololu A4988 [package=SO16]
  J2_Keypad_4x7 = double row male pin header, 6 pins [form="♂ (male)"]
  U1 = Voltage Regulator - 5V [package="TO220 [THT]"]
  100µF/50V = Electrolytic Capacitor [capacitance=0.1mF voltage=50V package="100 mil [THT, electrolytic]"]
  RJ45_Jack1 = RJ45 Jack [package=rj45-8]
  J2_Display_I2C27 = double row female pin header, 8 pins [form="♀ (female)"]
  J2_Display_I2C28 = female pin header, 4 pins [form="♀ (female)"]
  J2_Display_I2C29 = female pin header, 8 pins [form="♀ (female)"]
  J2_Display_I2C30 = female pin header, 4 pins [form="♀ (female)"]

nets:
  N1: Particle_Photon.A0, J2_Display_I2C29.pin8
  N2: Particle_Photon.A1, J2_Display_I2C29.pin7
  N3: Particle_Photon.A2, J2_Display_I2C29.pin6
  N4: Particle_Photon.A3, J2_Display_I2C29.pin5
  N5: Particle_Photon.A4, J2_Display_I2C29.pin4
  N6: Particle_Photon.A5, J2_Display_I2C29.pin3
  N7: Particle_Photon.DAC, J2_Display_I2C29.pin2
  N8: Particle_Photon.WKP, J2_Display_I2C29.pin1
  N9: Particle_Photon.RX, J2_Display_I2C30.pin2
  N10: Particle_Photon.TX, J2_Display_I2C30.pin3
  GND: Particle_Photon.GND, J2_Keypad_4x6.pin1, D2.anode, MD09B2.GND, J2_Keypad_4x7.pin1, J2_Keypad_4x7.pin2, J2_Keypad_4x7.pin3, U1.GND, 100µF/50V.-, J2_Display_I2C28.pin4, J2_Display_I2C30.pin1
  N11: Particle_Photon.VIN, MD09B2.RESET, MD09B2.SLEEP, J2_Keypad_4x7.pin4, J2_Keypad_4x7.pin5, J2_Keypad_4x7.pin6, U1.input_voltage, J2_Display_I2C28.pin3, J2_Display_I2C30.pin4
  N12: Particle_Photon.D0, J2_Display_I2C28.pin2
  N13: Particle_Photon.D1, J2_Display_I2C28.pin1
  N14: Particle_Photon.D2, MD09B2.DIR
  N15: Particle_Photon.D3, MD09B2.STEP
  N16: Particle_Photon.D4, MD09B2.MS3
  N17: Particle_Photon.D5, MD09B2.MS2
  N18: Particle_Photon.D6, MD09B2.MS1
  N19: Particle_Photon.D7, MD09B2.ENABLE
  N20: Particle_Photon.VBAT, J2_Keypad_4x6.pin2
  N21: Particle_Photon.RST, J2_Keypad_4x6.pin3
  N22: Particle_Photon.3V3, J2_Keypad_4x6.pin4
  N23: J11.pin1, MD09B2.1B
  N24: J11.pin2, MD09B2.1A
  N25: J12.pin1, MD09B2.2A
  N26: J12.pin2, MD09B2.2B
  N27: J13.pin1, D2.cathode
  N28: J13.pin2, MD09B2.VMOT, U1.output_voltage, 100µF/50V.+
  N29: RJ45_Jack1.1, J2_Display_I2C27.pin5
  N30: RJ45_Jack1.2, J2_Display_I2C27.pin4
  N31: RJ45_Jack1.3, J2_Display_I2C27.pin6
  N32: RJ45_Jack1.4, J2_Display_I2C27.pin3
  N33: RJ45_Jack1.5, J2_Display_I2C27.pin7
  N34: RJ45_Jack1.6, J2_Display_I2C27.pin2
  N35: RJ45_Jack1.7, J2_Display_I2C27.pin8
  N36: RJ45_Jack1.8, J2_Display_I2C27.pin1

notes:
  24VDC
  +
  -
  MOTOR
  I2C LCD
  A4
  A5/reset
  WKP
  DAC
  A0
  A1
  A2
  A3
  VBAT
  GND
  RST
  3V3
  24V
  5V
  MS2
  MS1
  SLP
  STP
  DIR
  MS3
  B1
  B2
  ENA
  VMT
  FLT
  (B-)
  (B+)
  (A+)
  (A-)
  black
  red
  blue
  green
  [  ]
  o
  1N4001
  Serial
  DRV8825
  RJ45
  P7
  P5
  P3
  P1
  P8
  P6
  P4
  P2
  SDA
  SCL
  TX
  RX
  Version 5b | June 25 2018
  Designed by Sebastian Kopf
  sebastian.kopf@colorado.edu
  Particle Photon & DRV8825
  Stepper Controller
